# Fritzing sketch board-01b (saved by Fritzing 0.9.3b)
circuit board: 8cm x 8cm
breadboards: 1

parts:
  I2C_2 = female pin header, 4 pins [form="♀ (female)"]
  I2C_3 = female pin header, 4 pins [form="♀ (female)"]
  I2C_4 = female pin header, 4 pins [form="♀ (female)"]
  1W_1 = female pin header, 3 pins [form="♀ (female)"]
  1W_3 = female pin header, 3 pins [form="♀ (female)"]
  1W_4 = female pin header, 3 pins [form="♀ (female)"]
  C1 = Capacitor Polarized [package=cpol-radial-1000uf-25v]
  R1 = Resistor [tolerance=±5% resistance=470 package=THT]
  WS2812 = female pin header, 3 pins [form="♀ (female)"]
  I2C_1 = female pin header, 4 pins [form="♀ (female)"]
  Power_plug1 = Power plug
  1W_2 = female pin header, 3 pins [form="♀ (female)"]
  Nano1 = Arduino Nano v2.3
  SPI = female pin header, 5 pins [form="♀ (female)"]
  IR1 = TSOP312.., 314.. [package=THT]
  LED1 = LED - 5mm [color="Infrared (940nm)" package="5 mm [THT]"]
  R2 = Resistor [tolerance=±5% resistance=330 package=THT]
  DHT = female pin header, 3 pins [form="♀ (female)"]
  D0 = female pin header, 3 pins [form="♀ (female)"]
  ADC0 = female pin header, 3 pins [form="♀ (female)"]
  J1 = female pin header, 15 pins [form="♀ (female)"]
  NE1 = female pin header, 15 pins [form="♀ (female)"]
  J2 = female pin header, 15 pins [form="♀ (female)"]
  J3 = female pin header, 15 pins [form="♀ (female)"]
  U1 = NodeMCU V1.0
  pin_fix_2 = female pin header, 15 pins [form="♀ (female)"]  # not connected
  pin_fix_1 = female pin header, 15 pins [form="♀ (female)"]  # not connected
  Part1 = Logic Level Converter
  R3 = Resistor [tolerance=±5% resistance=220 package=THT]
  LED2 = LED - 5mm [color="Red (633nm)" package="5 mm [THT]"]
  LED3 = LED - 5mm [color="Red (633nm)" package="5 mm [THT]"]
  R4 = Resistor [tolerance=±5% resistance=220 package=THT]
  IC1 = Voltage Regulator [package=to220-adj]
  D1 = Schottky Diode [part_number=1N5817 package="300 mil [THT]"]

nets:
  N1: I2C_2.pin1, I2C_3.pin1, I2C_4.pin1, 1W_1.pin1, 1W_3.pin1, 1W_4.pin1, I2C_1.pin1, 1W_2.pin1, SPI.pin1, DHT.pin1, D0.pin1, ADC0.pin3, J2.pin11, J3.pin6, J3.pin15, U1.3V3, Part1.LV, LED3.anode
  GND: I2C_2.pin2, I2C_3.pin2, I2C_4.pin2, 1W_1.pin3, 1W_3.pin3, 1W_4.pin3, C1.-, WS2812.pin3, I2C_1.pin2, Power_plug1.GND, 1W_2.pin3, Nano1.GND, SPI.pin2, IR1.Vs, LED1.anode, DHT.pin3, D0.pin2, ADC0.pin2, J1.pin12, NE1.pin14, J2.pin10, J2.pin14, J3.pin7, J3.pin14, U1.GND, Part1.GND, LED2.cathode, R4.Pin_1, IC1.ADJ
  N2: I2C_2.pin3, I2C_3.pin3, I2C_4.pin3, I2C_1.pin3, J3.pin4, U1.D3, Part1.RX2_LV
  N3: I2C_2.pin4, I2C_3.pin4, I2C_4.pin4, I2C_1.pin4, J3.pin3, U1.D2, Part1.TX2_LV
  N4: 1W_1.pin2, 1W_3.pin2, 1W_4.pin2, 1W_2.pin2, J3.pin2, U1.D1
  VIN: C1.+, WS2812.pin1, Nano1.VIN, NE1.pin15, J2.pin15, U1.Vin, R3.Pin_1, D1.cathode
  N5: R1.Pin_0, J3.pin5, U1.D4
  N6: R1.Pin_1, WS2812.pin2
  N7: Power_plug1.VCC, IC1.IN
  N8: Nano1.D1TX, J1.pin15
  N9: Nano1.D0RX, J1.pin14
  N10: Nano1.RST, J1.pin13, NE1.pin13
  N11: Nano1.D2, J1.pin11
  N12: Nano1.D3, R2.Pin_0, J1.pin10
  N13: Nano1.D4, J1.pin9
  N14: Nano1.D5, J1.pin8
  N15: Nano1.D6, J1.pin7
  N16: Nano1.D7, J1.pin6
  N17: Nano1.D8, J1.pin5
  N18: Nano1.D9, J1.pin4
  N19: Nano1.D10, J1.pin3
  N20: Nano1.D11, IR1.GND, J1.pin2
  N21: Nano1.D12, J1.pin1
  N22: Nano1.D13, NE1.pin1
  N23: Nano1.3V3, NE1.pin2
  N24: Nano1.AREF, NE1.pin3
  N25: Nano1.A7, NE1.pin4
  N26: Nano1.A6, NE1.pin5
  N27: Nano1.A5, NE1.pin6, Part1.RX2_HV
  N28: Nano1.A4, NE1.pin7, Part1.TX2_HV
  N29: Nano1.A3, NE1.pin8
  N30: Nano1.A2, NE1.pin9
  N31: Nano1.A1, NE1.pin10
  N32: Nano1.A0, NE1.pin11
  N33: Nano1.+5V, IR1.Data, NE1.pin12, Part1.HV
  N34: SPI.pin3, J3.pin10, U1.D7
  N35: SPI.pin4, J3.pin11, U1.D8
  N36: SPI.pin5, J3.pin8, U1.D5
  N37: LED1.cathode, R2.Pin_1
  N38: DHT.pin2, J3.pin9, U1.D6
  N39: D0.pin3, J3.pin1, U1.D0
  N40: ADC0.pin1, J2.pin1, U1.A0
  N41: J2.pin2, U1.RSV#41
  N42: J2.pin3, U1.RSV#40
  N43: J2.pin4, U1.SD3
  N44: J2.pin5, U1.SD2
  N45: J2.pin6, U1.SD1
  N46: J2.pin7, U1.CMD
  N47: J2.pin8, U1.SD0
  N48: J2.pin9, U1.CLK
  N49: J2.pin12, U1.EN
  N50: J2.pin13, U1.RST
  N51: J3.pin12, U1.RX
  N52: J3.pin13, U1.TX
  N53: R3.Pin_0, LED2.anode
  N54: LED3.cathode, R4.Pin_0
  N55: IC1.OUT, D1.anode

notes:
  3v3
  GND
  SCL
  SDA
  CS
  DAT
  CLK
  3v
  GN
  D6
  D0
  A0
  SPI
  ESP8266-12E
  NANO
  LLS
  DC
  WSH
  lan t
  rev   1.0b
  1-wire
  IR1
  D4
  5V
  VCC

custom parts:
  NodeMCU V1.0: ESP8266 based NodeMCU
