# Fritzing sketch cjmcu air adapter (saved by Fritzing 0.9.3b)
circuit board: 2.4cm x 1.5cm
breadboards: 1

parts:
  J2 = female pin header, 4 pins [form="♀ (female)"]
  J1 = female pin header, 8 pins [form="♀ (female)"]

nets:
  N1: J2.pin1, J1.pin1
  N2: J2.pin2, J1.pin3, J1.pin6
  N3: J2.pin3, J1.pin5
  N4: J2.pin4, J1.pin4

notes:
  GND
  VIN
  SDA
  SCL
  VCC
  <- board
  cjmcu ->
  3v3
  WAKE
  RST
  INT
