# Fritzing sketch direct adapter (saved by Fritzing 0.9.3b)
circuit board: 1.4cm x 1.5cm
breadboards: 1

parts:
  J1 = female pin header, 4 pins [form="♀ (female)"]
  J2 = female pin header, 4 pins [form="♀ (female)"]

nets:
  N1: J1.pin1, J2.pin1
  N2: J1.pin2, J2.pin2
  N3: J1.pin3, J2.pin3
  N4: J1.pin4, J2.pin4

notes:
  GND
  VCC
  SDA
  SCL
  <- board
  dev ->
